# Fritzing sketch wodowskaz (saved by Fritzing 0.7.5b)
breadboards: 1

parts:
  Arduino1 = Arduino
  SPKR1 = Loudspeaker
  U1 = mystery part, 4 pins [chip_label=HC-SR04 spacing=300mil part_number=HC-SR04]

nets:
  N1: Arduino1.GND, SPKR1.pin1, U1.pin4
  N2: Arduino1.D10, U1.pin3
  N3: Arduino1.D9, U1.pin2
  N4: Arduino1.D3, SPKR1.pin2
  N5: Arduino1.+5V, U1.pin1
